# Fritzing sketch Rasp (saved by Fritzing 0.9.3b)
breadboards: 1

parts:
  Raspberry_Pi_1 = Raspberry Pi 3 [part_number=RPI-3-V1.2]  # not connected
  Part1 = Adafruit Pi Cobbler Plus [part_number="Adafruit #2029"]  # not connected
  KEYPAD3 = Membrane Matrix Keypad  # not connected
  U2 = LCD-16X2 [package=lcd-16x2_noholes]
  U4 = POT [package=pot_mammoth]
  M1 = Dagu DGServo 9g (End View) [part_number=RS001B]
  U5 = SWITCH_SPDT [package=kps-1290]
  BAT1 = Battery Holders [package=battery-aa]
  BAT2 = Battery Holders [package=battery-aa]
  BAT3 = Battery Holders [package=battery-aa]
  BAT4 = Battery Holders [package=battery-aa]
  BAT5 = Battery Holders [package=battery-aa]

nets:
  VSS: U2.VSS, U2.R_W, U4.S, M1.gnd, BAT5.+
  N1: U2.VDD, U4.E
  N2: U2.VO, U4.A
  N3: M1.vcc, U5.P
  N4: U5.O, BAT1.-
  N5: BAT1.+, BAT2.-
  N6: BAT2.+, BAT3.-
  N7: BAT3.+, BAT4.-
  N8: BAT4.+, BAT5.-

custom parts:
  Adafruit Pi Cobbler Plus: The Raspberry Pi B+/Pi 2/ Pi 3 has landed on the Maker World like a 40-GPIO pinned, quad-USB ported, credit card sized bomb of DIY joy. And while you can use most of our great Model B accessories by hooking up our downgrade cable, its probably a good time to upgrade your set up and accessorize using all of the Model B+'s / Pi 2's / Pi 3's 40 pins. That's why we now carry the Adafruit Assembled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
  Membrane Matrix Keypad: Membrane Matrix 3x4 Keypad
